// Logisim project single-cycle-cpu.circ as structural Verilog: 12 circuits, main circuit main
module main (
  input  in_1,
  output [5:0] out_2,
  output [5:0] out_3
);

  wire ALUsrc, clk, J, MemtoReg, MemWrite, nPC_sel, RegDst, RegWrite, zero;
  wire [1:0] ALUctrl, Extop;
  wire [4:0] multiplexer_1_out, rs, rt;
  wire [7:0] n20074221_ifu_1_pcaddress;
  wire [15:6] immediate;
  wire [31:0] multiplexer_2_out, multiplexer_3_out, n20074221_alu_1_out, n20074221_dm_1_data_out,
       n20074221_ext_1_ext32, n20074221_gpr_1_out1, n20074221_gpr_1_out2;

  // Probe on n20074221_ifu_1_pcaddress
  _20074221_IFU u_20074221_ifu_1 (
    .npc_sel(nPC_sel), .zero(zero), .ins({out_2, rs, rt, immediate, out_3}),
    .PCaddress(n20074221_ifu_1_pcaddress), .J(J), .clk(clk), .reset(in_1));
  Clock #(.highDuration(1), .lowDuration(1)) clock_1 (.out(clk));
  // Probe on {out_2, rs, rt, immediate, out_3}
  _20074221_GPR u_20074221_gpr_1 (
    .clk(clk), .reset(in_1), .regWrite(RegWrite), .out1(n20074221_gpr_1_out1), .out2(n20074221_gpr_1_out2),
    .Busw(multiplexer_3_out), .reg3(multiplexer_1_out), .rs(rs), .rt(rt));
  Multiplexer #(.select(1), .width(5), .disabled("Z"), .enable("false")) multiplexer_1 (
    .in0(rt), .in1(immediate[15:11]), .out(multiplexer_1_out), .sel(RegDst));
  _20074221_EXT u_20074221_ext_1 (.imm16({immediate, out_3}), .ExtOp(Extop), .ext32(n20074221_ext_1_ext32));
  _20074221_Control u_20074221_control_1 (
    .func(out_3), .opcode(out_2), .RegDst(RegDst), .ALUsrc(ALUsrc), .MemtoReg(MemtoReg), .RegWrite(RegWrite),
    .MemWrite(MemWrite), .nPC_sel(nPC_sel), .Extop(Extop), .ALUctrl(ALUctrl), .J(J));
  Multiplexer #(.select(1), .width(32), .disabled("Z"), .enable("false")) multiplexer_2 (
    .in0(n20074221_gpr_1_out2), .in1(n20074221_ext_1_ext32), .out(multiplexer_2_out), .sel(ALUsrc));
  Multiplexer #(.select(1), .width(32), .disabled("Z"), .enable("false")) multiplexer_3 (
    .in0(n20074221_alu_1_out), .in1(n20074221_dm_1_data_out), .out(multiplexer_3_out), .sel(MemtoReg));
  _20074221_ALU u_20074221_alu_1 (
    .A(n20074221_gpr_1_out1), .B(multiplexer_2_out), .ALUctr(ALUctrl), .out(n20074221_alu_1_out), .zero(zero));
  _20074221_DM u_20074221_dm_1 (
    .address(n20074221_alu_1_out[9:0]), .DATA_IN(n20074221_gpr_1_out2), .MemWr(MemWrite), .clk(clk),
    .reset(in_1), .DATA_OUT(n20074221_dm_1_data_out));

  // Other names for the same wires on the sheet: func[5:0] = out_3; immediate[5:0] = out_3; opcode[5:0] = out_2;
  //   rd[4:0] = immediate[15:11]; reset = in_1; shamet[4:0] = immediate[10:6]

  // Notes on the sheet:
  //   低位
  //   func
  //   shamet
  //   rd
  //   rt
  //   rs
  //   opcode
  //   高位
endmodule

// IFU
module _20074221_IFU (
  input  J,
  input  npc_sel,
  input  zero,
  input  clk,
  input  reset,
  output [7:0] PCaddress,
  output [31:0] ins
);

  wire _28, _29, _30, _31, and_1_out;
  wire [27:0] PC_q;
  wire [31:0] adder_1_out, adder_2_out, bit_extender_1_out, multiplexer_1_out, multiplexer_2_out,
       shifter_1_out;

  assign bit_extender_1_out = {{16{ins[15]}}, ins[15:0]};  // Bit_Extender bit_extender_1
  Shifter #(.width(32), .shift("ll")) shifter_1 (.in(bit_extender_1_out), .\dist (5'b00010), .out(shifter_1_out));
  Adder #(.width(32)) adder_1 (
    .a({_31, _30, _29, _28, PC_q[27:10], PCaddress, PC_q[1:0]}), .b(32'h4), .out(adder_1_out));  // open: cin, cout
  Adder #(.width(32)) adder_2 (.a(adder_1_out), .b(shifter_1_out), .out(adder_2_out));  // open: cin, cout
  Multiplexer #(.select(1), .width(32), .disabled("Z"), .enable("false")) multiplexer_1 (
    .in0(adder_1_out), .in1(adder_2_out), .out(multiplexer_1_out), .sel(and_1_out));
  and and_1 (and_1_out, npc_sel, zero);
  Multiplexer #(.select(1), .width(32), .disabled("Z"), .enable("false")) multiplexer_2 (
    .in0(multiplexer_1_out), .in1({_31, _30, _29, _28, ins[25:0], 2'b00}), .out(multiplexer_2_out), .sel(J));
  Register #(.width(32), .trigger("rising"), .Select("low")) PC (
    .D(multiplexer_2_out), .Q({_31, _30, _29, _28, PC_q[27:10], PCaddress, PC_q[1:0]}), .clk(clk), .clr(reset));  // open: en
  ROM #(.addrWidth(8), .dataWidth(8), .Select("low")) ROM_3 (.addr(PCaddress), .data(ins[31:24]));
  ROM #(.addrWidth(8), .dataWidth(8), .Select("low")) ROM_2 (.addr(PCaddress), .data(ins[23:16]));
  ROM #(.addrWidth(8), .dataWidth(8), .Select("low")) ROM_1 (.addr(PCaddress), .data(ins[15:8]));
  ROM #(.addrWidth(8), .dataWidth(8), .Select("low")) ROM_0 (.addr(PCaddress), .data(ins[7:0]));
  // Probe on ins

  // Other names for the same wires on the sheet: imm[15:0] = ins[15:0];
  //   J_code[31:2] = {_31, _30, _29, _28, ins[25:0]}

  // Notes on the sheet:
  //   PC+4
  //   用于判断是beq还是PC+4
  //   判断是否是J指令
  //   contents of ROM_3 (hex, n*v repeats v):
  //   34 34 0 0 1 ac 8c 11 3c 8 34 3c 8
  //   contents of ROM_2 (hex, n*v repeats v):
  //   3 6 66 66 2a 9 a 2a b 0 b 9
  //   contents of ROM_1 (hex, n*v repeats v):
  //   0 0 40 48 4*0 cd c ef 45 c
  //   contents of ROM_0 (hex, n*v repeats v):
  //   93 ae 21 23 21 10 10 2 cd d ef 67 7
endmodule

// CONTROLLER
module _20074221_Control (
  input  [5:0] func,
  input  [5:0] opcode,
  output RegDst,
  output ALUsrc,
  output MemtoReg,
  output RegWrite,
  output MemWrite,
  output nPC_sel,
  output [1:0] Extop,
  output [1:0] ALUctrl,
  output J
);

  wire addu_out, beq_out, j_out, lw_out, not_1_out, not_2_out, not_3_out, not_4_out, not_5_out, not_6_out,
       not_7_out, not_8_out, not_9_out, not_10_out, not_11_out, not_12_out, ori_out, subu_out, sw_out;

  not not_1 (not_1_out, func[5]);
  not not_2 (not_2_out, func[3]);
  not not_3 (not_3_out, func[4]);
  not not_4 (not_4_out, func[1]);
  not not_5 (not_5_out, func[2]);
  not not_6 (not_6_out, func[0]);
  not not_7 (not_7_out, opcode[5]);
  not not_8 (not_8_out, opcode[3]);
  not not_9 (not_9_out, opcode[4]);
  not not_10 (not_10_out, opcode[2]);
  not not_11 (not_11_out, opcode[1]);
  not not_12 (not_12_out, opcode[0]);
  and addu (addu_out, func[5], not_3_out, not_2_out, not_5_out, not_4_out, func[0], not_7_out, not_9_out, not_8_out, not_10_out, not_11_out, not_12_out);
  and subu (subu_out, func[5], not_3_out, not_2_out, not_5_out, func[1], func[0], not_7_out, not_9_out, not_8_out, not_10_out, not_11_out, not_12_out);
  and ori (ori_out, not_7_out, not_9_out, opcode[3], opcode[2], not_11_out, opcode[0]);
  and lw (lw_out, opcode[5], not_9_out, not_8_out, not_10_out, opcode[1], opcode[0]);
  and sw (sw_out, opcode[5], not_9_out, opcode[3], not_10_out, opcode[1], opcode[0]);
  and lui (Extop[1], not_7_out, not_9_out, opcode[3], opcode[2], opcode[1], opcode[0]);
  and u_j (j_out, not_7_out, not_9_out, not_8_out, not_10_out, opcode[1], not_12_out);
  and beq (beq_out, not_7_out, not_9_out, not_8_out, opcode[2], not_11_out, not_12_out);
  or or_1 (RegDst, addu_out, subu_out);
  or or_2 (ALUsrc, ori_out, lw_out, sw_out, Extop[1]);
  buf or_3 (MemtoReg, lw_out);  // OR_Gate
  or or_4 (RegWrite, addu_out, subu_out, Extop[1], ori_out, lw_out);
  buf or_5 (MemWrite, sw_out);  // OR_Gate
  buf or_6 (nPC_sel, beq_out);  // OR_Gate
  or or_7 (Extop[0], lw_out, sw_out);
  or or_8 (ALUctrl[1], addu_out, lw_out, sw_out);
  or or_9 (ALUctrl[0], subu_out, beq_out);
  buf J_2 (J, j_out);  // OR_Gate

  // Notes on the sheet:
  //   RegDst
  //   ALUsrc
  //   MemtoReg
  //   RegWrite
  //   MemWrite
  //   nPC_sel
  //   ExtOp
  //   00     0拓展
  //   01 符号拓展
  //   00 lui的拓展
  //   ALUctrl
  //   00     ori
  //   01 subu
  //   10  addu
endmodule

// Regfile
module _20074221_GPR (
  input  [31:0] Busw,
  input  clk,
  input  reset,
  input  [4:0] rs,
  input  regWrite,
  input  [4:0] reg3,
  input  [4:0] rt,
  output [31:0] out1,
  output [31:0] out2
);

  wire demultiplexer_1_out0, demultiplexer_1_out1, demultiplexer_1_out2, demultiplexer_1_out3,
       demultiplexer_1_out4, demultiplexer_1_out5, demultiplexer_1_out6, demultiplexer_1_out7,
       demultiplexer_1_out8, demultiplexer_1_out9, demultiplexer_1_out10, demultiplexer_1_out11,
       demultiplexer_1_out12, demultiplexer_1_out13, demultiplexer_1_out14, demultiplexer_1_out15,
       demultiplexer_1_out16, demultiplexer_1_out17, demultiplexer_1_out18, demultiplexer_1_out19,
       demultiplexer_1_out20, demultiplexer_1_out21, demultiplexer_1_out22, demultiplexer_1_out23,
       demultiplexer_1_out24, demultiplexer_1_out25, demultiplexer_1_out26, demultiplexer_1_out27,
       demultiplexer_1_out28, demultiplexer_1_out29, demultiplexer_1_out30, demultiplexer_1_out31;
  wire [31:0] _0, _1, _2, _3, _4, _5, _6, _7, _8, _9, _10, _11, _12, _13, _14, _15, _16, _17, _18, _19, _20,
       _21, _22, _23, _24, _25, _26, _27, _28, _29, _30, _31;

  Demultiplexer #(.select(5), .width(1), .tristate("false"), .disabled("Z"), .enable("false")) demultiplexer_1 (
    .out0(demultiplexer_1_out0), .out1(demultiplexer_1_out1), .out2(demultiplexer_1_out2),
    .out3(demultiplexer_1_out3), .out4(demultiplexer_1_out4), .out5(demultiplexer_1_out5),
    .out6(demultiplexer_1_out6), .out7(demultiplexer_1_out7), .out8(demultiplexer_1_out8),
    .out9(demultiplexer_1_out9), .out10(demultiplexer_1_out10), .out11(demultiplexer_1_out11),
    .out12(demultiplexer_1_out12), .out13(demultiplexer_1_out13), .out14(demultiplexer_1_out14),
    .out15(demultiplexer_1_out15), .out16(demultiplexer_1_out16), .out17(demultiplexer_1_out17),
    .out18(demultiplexer_1_out18), .out19(demultiplexer_1_out19), .out20(demultiplexer_1_out20),
    .out21(demultiplexer_1_out21), .out22(demultiplexer_1_out22), .out23(demultiplexer_1_out23),
    .out24(demultiplexer_1_out24), .out25(demultiplexer_1_out25), .out26(demultiplexer_1_out26),
    .out27(demultiplexer_1_out27), .out28(demultiplexer_1_out28), .out29(demultiplexer_1_out29),
    .out30(demultiplexer_1_out30), .out31(demultiplexer_1_out31), .in(regWrite), .sel(reg3));
  Register #(.width(32), .trigger("rising"), .Select("low")) register_1 (
    .D({32{1'b0}}), .en(demultiplexer_1_out0), .Q(_0), .clk(clk), .clr(reset));
  Register #(.width(32), .trigger("rising"), .Select("low")) register_2 (
    .D(Busw), .en(demultiplexer_1_out1), .Q(_1), .clk(clk), .clr(reset));
  Register #(.width(32), .trigger("rising"), .Select("low")) register_3 (
    .D(Busw), .en(demultiplexer_1_out2), .Q(_2), .clk(clk), .clr(reset));
  Register #(.width(32), .trigger("rising"), .Select("low")) register_4 (
    .D(Busw), .en(demultiplexer_1_out3), .Q(_3), .clk(clk), .clr(reset));
  Register #(.width(32), .trigger("rising"), .Select("low")) register_5 (
    .D(Busw), .en(demultiplexer_1_out4), .Q(_4), .clk(clk), .clr(reset));
  Register #(.width(32), .trigger("rising"), .Select("low")) register_6 (
    .D(Busw), .en(demultiplexer_1_out5), .Q(_5), .clk(clk), .clr(reset));
  Register #(.width(32), .trigger("rising"), .Select("low")) register_7 (
    .D(Busw), .en(demultiplexer_1_out6), .Q(_6), .clk(clk), .clr(reset));
  Register #(.width(32), .trigger("rising"), .Select("low")) register_8 (
    .D(Busw), .en(demultiplexer_1_out7), .Q(_7), .clk(clk), .clr(reset));
  Register #(.width(32), .trigger("rising"), .Select("low")) register_9 (
    .D(Busw), .en(demultiplexer_1_out8), .Q(_8), .clk(clk), .clr(reset));
  Register #(.width(32), .trigger("rising"), .Select("low")) register_10 (
    .D(Busw), .en(demultiplexer_1_out9), .Q(_9), .clk(clk), .clr(reset));
  Register #(.width(32), .trigger("rising"), .Select("low")) register_11 (
    .D(Busw), .en(demultiplexer_1_out10), .Q(_10), .clk(clk), .clr(reset));
  Register #(.width(32), .trigger("rising"), .Select("low")) register_12 (
    .D(Busw), .en(demultiplexer_1_out11), .Q(_11), .clk(clk), .clr(reset));
  Register #(.width(32), .trigger("rising"), .Select("low")) register_13 (
    .D(Busw), .en(demultiplexer_1_out12), .Q(_12), .clk(clk), .clr(reset));
  Register #(.width(32), .trigger("rising"), .Select("low")) register_14 (
    .D(Busw), .en(demultiplexer_1_out13), .Q(_13), .clk(clk), .clr(reset));
  Register #(.width(32), .trigger("rising"), .Select("low")) register_15 (
    .D(Busw), .en(demultiplexer_1_out14), .Q(_14), .clk(clk), .clr(reset));
  Register #(.width(32), .trigger("rising"), .Select("low")) register_16 (
    .D(Busw), .en(demultiplexer_1_out15), .Q(_15), .clk(clk), .clr(reset));
  Register #(.width(32), .trigger("rising"), .Select("low")) register_17 (
    .D(Busw), .en(demultiplexer_1_out16), .Q(_16), .clk(clk), .clr(reset));
  Register #(.width(32), .trigger("rising"), .Select("low")) register_18 (
    .D(Busw), .en(demultiplexer_1_out17), .Q(_17), .clk(clk), .clr(reset));
  Register #(.width(32), .trigger("rising"), .Select("low")) register_19 (
    .D(Busw), .en(demultiplexer_1_out18), .Q(_18), .clk(clk), .clr(reset));
  Register #(.width(32), .trigger("rising"), .Select("low")) register_20 (
    .D(Busw), .en(demultiplexer_1_out19), .Q(_19), .clk(clk), .clr(reset));
  Register #(.width(32), .trigger("rising"), .Select("low")) register_21 (
    .D(Busw), .en(demultiplexer_1_out20), .Q(_20), .clk(clk), .clr(reset));
  Register #(.width(32), .trigger("rising"), .Select("low")) register_22 (
    .D(Busw), .en(demultiplexer_1_out21), .Q(_21), .clk(clk), .clr(reset));
  Register #(.width(32), .trigger("rising"), .Select("low")) register_23 (
    .D(Busw), .en(demultiplexer_1_out22), .Q(_22), .clk(clk), .clr(reset));
  Register #(.width(32), .trigger("rising"), .Select("low")) register_24 (
    .D(Busw), .en(demultiplexer_1_out23), .Q(_23), .clk(clk), .clr(reset));
  Register #(.width(32), .trigger("rising"), .Select("low")) register_25 (
    .D(Busw), .en(demultiplexer_1_out24), .Q(_24), .clk(clk), .clr(reset));
  Register #(.width(32), .trigger("rising"), .Select("low")) register_26 (
    .D(Busw), .en(demultiplexer_1_out25), .Q(_25), .clk(clk), .clr(reset));
  Register #(.width(32), .trigger("rising"), .Select("low")) register_27 (
    .D(Busw), .en(demultiplexer_1_out26), .Q(_26), .clk(clk), .clr(reset));
  Register #(.width(32), .trigger("rising"), .Select("low")) register_28 (
    .D(Busw), .en(demultiplexer_1_out27), .Q(_27), .clk(clk), .clr(reset));
  Register #(.width(32), .trigger("rising"), .Select("low")) register_29 (
    .D(Busw), .en(demultiplexer_1_out28), .Q(_28), .clk(clk), .clr(reset));
  Register #(.width(32), .trigger("rising"), .Select("low")) register_30 (
    .D(Busw), .en(demultiplexer_1_out29), .Q(_29), .clk(clk), .clr(reset));
  Register #(.width(32), .trigger("rising"), .Select("low")) register_31 (
    .D(Busw), .en(demultiplexer_1_out30), .Q(_30), .clk(clk), .clr(reset));
  Register #(.width(32), .trigger("rising"), .Select("low")) register_32 (
    .D(Busw), .en(demultiplexer_1_out31), .Q(_31), .clk(clk), .clr(reset));
  Multiplexer #(.select(5), .width(32), .disabled("Z"), .enable("false")) multiplexer_1 (
    .in0(_0), .in1(_1), .in2(_2), .in3(_3), .in4(_4), .in5(_5), .in6(_6), .in7(_7), .in8(_8), .in9(_9),
    .in10(_10), .in11(_11), .in12(_12), .in13(_13), .in14(_14), .in15(_15), .in16(_16), .in17(_17),
    .in18(_18), .in19(_19), .in20(_20), .in21(_21), .in22(_22), .in23(_23), .in24(_24), .in25(_25),
    .in26(_26), .in27(_27), .in28(_28), .in29(_29), .in30(_30), .in31(_31), .out(out1), .sel(rs));
  Multiplexer #(.select(5), .width(32), .disabled("Z"), .enable("false")) multiplexer_2 (
    .in0(_0), .in1(_1), .in2(_2), .in3(_3), .in4(_4), .in5(_5), .in6(_6), .in7(_7), .in8(_8), .in9(_9),
    .in10(_10), .in11(_11), .in12(_12), .in13(_13), .in14(_14), .in15(_15), .in16(_16), .in17(_17),
    .in18(_18), .in19(_19), .in20(_20), .in21(_21), .in22(_22), .in23(_23), .in24(_24), .in25(_25),
    .in26(_26), .in27(_27), .in28(_28), .in29(_29), .in30(_30), .in31(_31), .out(out2), .sel(rt));

  // Notes on the sheet:
  //   reg3表示要写入的寄存器编号
  //   output
  //   $zero
  //   $at
  //   $v0
  //   $v1
  //   $a0
  //   $a1
  //   $a2
  //   $a3
  //   $t0
  //   $t1
  //   $t2
  //   $t3
  //   $t4
  //   $t5
  //   $t6
  //   $t7
  //   $s0
  //   $s1
  //   $s2
  //   $s3
  //   $s4
  //   $s5
  //   $s6
  //   $s7
  //   $t8
  //   $t9
  //   $k0
  //   $k1
  //   $gp
  //   $sp
  //   $fp
  //   $ra
  //   rs代表要读内容的寄存器编号
  //   rt代表要读内容的寄存器编号
endmodule

// ALU
module _20074221_ALU (
  input  [31:0] A,
  input  [31:0] B,
  input  [1:0] ALUctr,
  output zero,
  output [31:0] out
);

  wire [31:0] n20074221_add32_1_sum, n20074221_ori32_1_result, n20074221_sub32_1_result;

  _20074221_add32 u_20074221_add32_1 (.B(B), .A(A), .Sum(n20074221_add32_1_sum));  // open: out_3
  _20074221_sub32 u_20074221_sub32_1 (.A(A), .result(n20074221_sub32_1_result), .B(B));
  _20074221_ori32 u_20074221_ori32_1 (.A(A), .B(B), .result(n20074221_ori32_1_result));
  Multiplexer #(.select(2), .width(32), .disabled("Z"), .enable("true")) multiplexer_1 (
    .in0(n20074221_ori32_1_result), .in1(n20074221_sub32_1_result), .in2(n20074221_add32_1_sum), .out(out),
    .sel(ALUctr));  // open: in3, en
  Comparator #(.width(32), .mode("twosComplement")) comparator_1 (.a(out), .b({32{1'b0}}), .eq(zero));  // open: gt, lt

  // Notes on the sheet:
  //   00  or 
  //   01 sub 
  //   10 add 
endmodule

// DM
module _20074221_DM (
  input  MemWr,
  input  clk,
  input  reset,
  input  [9:0] address,
  input  [31:0] DATA_IN,
  output [31:0] DATA_OUT
);

  wire [9:0] shifter_1_out;

  Shifter #(.width(10), .shift("lr")) shifter_1 (.in(address), .\dist (4'b0010), .out(shifter_1_out));
  RAM #(.addrWidth(10), .dataWidth(8), .bus("separate"), .Select("low")) DM3 (
    .addr(shifter_1_out), .din(DATA_IN[7:0]), .data(DATA_OUT[7:0]), .str(MemWr), .clk(clk), .clr(reset));  // open: sel, ld
  RAM #(.addrWidth(10), .dataWidth(8), .bus("separate"), .Select("low")) DM2 (
    .addr(shifter_1_out), .din(DATA_IN[15:8]), .data(DATA_OUT[15:8]), .str(MemWr), .clk(clk), .clr(reset));  // open: sel, ld
  RAM #(.addrWidth(10), .dataWidth(8), .bus("separate"), .Select("low")) DM1 (
    .addr(shifter_1_out), .din(DATA_IN[23:16]), .data(DATA_OUT[23:16]), .str(MemWr), .clk(clk), .clr(reset));  // open: sel, ld
  RAM #(.addrWidth(10), .dataWidth(8), .bus("separate"), .Select("low")) DM0 (
    .addr(shifter_1_out), .din(DATA_IN[31:24]), .data(DATA_OUT[31:24]), .str(MemWr), .clk(clk), .clr(reset));  // open: sel, ld
endmodule

// EXT
module _20074221_EXT (
  input  [15:0] imm16,
  input  [1:0] ExtOp,
  output [31:0] ext32
);

  wire [31:0] bit_extender_1_out, bit_extender_2_out;

  assign bit_extender_1_out = {{16{1'b0}}, imm16};  // Bit_Extender bit_extender_1
  assign bit_extender_2_out = {{16{imm16[15]}}, imm16};  // Bit_Extender bit_extender_2
  Multiplexer #(.select(2), .width(32), .disabled("Z"), .enable("false")) multiplexer_1 (
    .in0(bit_extender_1_out), .in1(bit_extender_2_out), .in2({imm16, {16{1'b0}}}), .out(ext32), .sel(ExtOp));  // open: in3

  // Notes on the sheet:
  //   00    0拓展
  //   01 符号拓展
  //   10  lui高位复制
endmodule

// add
module _20074221_add32 (
  input  [31:0] B,
  input  [31:0] A,
  output out_3,
  output [31:0] Sum
);

  wire and_1_out, G0_star, n20074221_add16_2_p0_star;

  _20074221_add16 u_20074221_add16_1 (
    .out15(Sum[31]), .out14(Sum[30]), .out13(Sum[29]), .out12(Sum[28]), .out11(Sum[27]), .out10(Sum[26]),
    .out9(Sum[25]), .out8(Sum[24]), .out7(Sum[23]), .out6(Sum[22]), .out5(Sum[21]), .out4(Sum[20]),
    .out3(Sum[19]), .out2(Sum[18]), .out1(Sum[17]), .out0(Sum[16]), .a15(A[31]), .b15(B[31]), .a14(A[30]),
    .b14(B[30]), .a13(A[29]), .b13(B[29]), .a12(A[28]), .b12(B[28]), .a11(A[27]), .b11(B[27]), .a10(A[26]),
    .b10(B[26]), .a9(A[25]), .b9(B[25]), .a8(A[24]), .b8(B[24]), .a7(A[23]), .b7(B[23]), .a6(A[22]),
    .b6(B[22]), .a5(A[21]), .b5(B[21]), .a4(A[20]), .b4(B[20]), .a3(A[19]), .b3(B[18]), .a2(A[18]),
    .b2(B[17]), .a1(A[17]), .b1(B[17]), .a0(A[16]), .b0(B[16]), .C0(out_3));  // open: G0_star, P0_star
  or or_1 (out_3, G0_star, and_1_out);
  and and_1 (and_1_out, n20074221_add16_2_p0_star, 1'b0);
  _20074221_add16 u_20074221_add16_2 (
    .G0_star(G0_star), .P0_star(n20074221_add16_2_p0_star), .out15(Sum[15]), .out14(Sum[14]),
    .out13(Sum[13]), .out12(Sum[12]), .out11(Sum[11]), .out10(Sum[10]), .out9(Sum[9]), .out8(Sum[8]),
    .out7(Sum[7]), .out6(Sum[6]), .out5(Sum[5]), .out4(Sum[4]), .out3(Sum[3]), .out2(Sum[2]), .out1(Sum[1]),
    .out0(Sum[0]), .a15(A[15]), .b15(B[15]), .a14(A[14]), .b14(B[14]), .a13(A[13]), .b13(B[13]), .a12(A[12]),
    .b12(B[12]), .a11(A[11]), .b11(B[11]), .a10(A[10]), .b10(B[10]), .a9(A[9]), .b9(B[9]), .a8(A[8]),
    .b8(B[8]), .a7(A[7]), .b7(B[7]), .a6(A[6]), .b6(B[6]), .a5(A[5]), .b5(B[5]), .a4(A[4]), .b4(B[4]),
    .a3(A[3]), .b3(B[3]), .a2(A[2]), .b2(B[2]), .a1(A[1]), .b1(B[1]), .a0(A[0]), .b0(B[0]), .C0(1'b0));

  // Other names for the same wires on the sheet: C1 = out_3
endmodule

// sub
module _20074221_sub32 (
  input  [31:0] A,
  input  [31:0] B,
  output [31:0] result
);

  wire [31:0] n20074221_add32_2_sum, not_1_out;

  _20074221_add32 u_20074221_add32_1 (.B(n20074221_add32_2_sum), .A(A), .Sum(result));  // open: out_3
  _20074221_add32 u_20074221_add32_2 (.B(32'h1), .A(not_1_out), .Sum(n20074221_add32_2_sum));  // open: out_3
  assign not_1_out = ~B;  // NOT_Gate not_1, 32 bits wide
endmodule

// ori
module _20074221_ori32 (
  input  [31:0] A,
  input  [31:0] B,
  output [31:0] result
);

  assign result = A | B;  // OR_Gate or_1, 32 bits wide
endmodule

module _20074221_add16 (
  input  C0,
  input  b15,
  input  b14,
  input  b13,
  input  b12,
  input  b11,
  input  b10,
  input  b9,
  input  b8,
  input  b7,
  input  b6,
  input  b5,
  input  b4,
  input  b3,
  input  b2,
  input  b1,
  input  b0,
  input  a15,
  input  a14,
  input  a13,
  input  a12,
  input  a11,
  input  a10,
  input  a9,
  input  a8,
  input  a7,
  input  a6,
  input  a5,
  input  a4,
  input  a3,
  input  a2,
  input  a1,
  input  a0,
  output G0_star,
  output P0_star,
  output out14,
  output out10,
  output out6,
  output out2,
  output out13,
  output out9,
  output out5,
  output out1,
  output out15,
  output out12,
  output out11,
  output out8,
  output out7,
  output out4,
  output out3,
  output out0
);

  wire and_1_out, and_2_out, and_3_out, and_5_out, and_6_out, and_7_out, and_8_out, and_9_out, and_10_out,
       C4, C8, C12, n20074221_add4_1_g0_star, n20074221_add4_1_p0_star, n20074221_add4_2_g0_star,
       n20074221_add4_2_p0_star, n20074221_add4_3_g0_star, n20074221_add4_3_p0_star,
       n20074221_add4_4_g0_star, n20074221_add4_4_p0_star;

  or or_1 (G0_star, n20074221_add4_1_g0_star, and_2_out, and_1_out, and_3_out);
  and and_1 (and_1_out, n20074221_add4_1_p0_star, n20074221_add4_2_p0_star, n20074221_add4_3_g0_star);
  and and_2 (and_2_out, n20074221_add4_1_p0_star, n20074221_add4_2_g0_star);
  and and_3 (and_3_out, n20074221_add4_1_p0_star, n20074221_add4_2_p0_star, n20074221_add4_3_p0_star, n20074221_add4_4_g0_star);
  _20074221_add4 u_20074221_add4_1 (
    .G0_star(n20074221_add4_1_g0_star), .P0_star(n20074221_add4_1_p0_star), .out3(out15), .out2(out14),
    .out1(out13), .out0(out12), .a3(a15), .b3(b15), .a2(a14), .b2(b14), .a1(a13), .b1(b13), .a0(a12),
    .b0(b12), .C0(C12));
  and and_4 (P0_star, n20074221_add4_1_p0_star, n20074221_add4_2_p0_star, n20074221_add4_3_p0_star, n20074221_add4_4_p0_star);
  and and_5 (and_5_out, n20074221_add4_2_p0_star, n20074221_add4_3_g0_star);
  or or_2 (C12, n20074221_add4_2_g0_star, and_5_out, and_6_out, and_7_out);
  and and_6 (and_6_out, n20074221_add4_2_p0_star, n20074221_add4_3_p0_star, n20074221_add4_4_g0_star);
  _20074221_add4 u_20074221_add4_2 (
    .G0_star(n20074221_add4_2_g0_star), .P0_star(n20074221_add4_2_p0_star), .out3(out11), .out2(out10),
    .out1(out9), .out0(out8), .a3(a11), .b3(b11), .a2(a10), .b2(b10), .a1(a9), .b1(b9), .a0(a8), .b0(b8),
    .C0(C8));
  and and_7 (and_7_out, n20074221_add4_2_p0_star, n20074221_add4_3_p0_star, n20074221_add4_4_p0_star, C0);
  or or_3 (C8, n20074221_add4_3_g0_star, and_8_out, and_9_out);
  and and_8 (and_8_out, n20074221_add4_3_p0_star, n20074221_add4_4_g0_star);
  and and_9 (and_9_out, n20074221_add4_3_p0_star, n20074221_add4_4_p0_star, C0);
  _20074221_add4 u_20074221_add4_3 (
    .G0_star(n20074221_add4_3_g0_star), .P0_star(n20074221_add4_3_p0_star), .out3(out7), .out2(out6),
    .out1(out5), .out0(out4), .a3(a7), .b3(b7), .a2(a6), .b2(b6), .a1(a5), .b1(b5), .a0(a4), .b0(b4), .C0(C4));
  or or_4 (C4, n20074221_add4_4_g0_star, and_10_out);
  and and_10 (and_10_out, n20074221_add4_4_p0_star, C0);
  _20074221_add4 u_20074221_add4_4 (
    .G0_star(n20074221_add4_4_g0_star), .P0_star(n20074221_add4_4_p0_star), .out3(out3), .out2(out2),
    .out1(out1), .out0(out0), .a3(a3), .b3(b3), .a2(a2), .b2(b2), .a1(a1), .b1(b1), .a0(a0), .b0(b0), .C0(C0));
endmodule

module _20074221_add4 (
  input  C0,
  input  a0,
  input  b0,
  input  a1,
  input  b1,
  input  a3,
  input  b3,
  input  a2,
  input  b2,
  output G0_star,
  output P0_star,
  output out3,
  output out2,
  output out1,
  output out0
);

  wire and_1_out, and_2_out, and_3_out, and_5_out, and_6_out, and_7_out, and_8_out, and_9_out, and_10_out,
       C1_out, C2_out, C3_out, G0_out, G1_out, G2_out, G3_out, P0_out, P1_out, P2_out, P3_out;

  and G3 (G3_out, a3, b3);
  or or_1 (G0_star, G3_out, and_1_out, and_2_out, and_3_out);
  and and_1 (and_1_out, P3_out, G2_out);
  and and_2 (and_2_out, P3_out, P2_out, G1_out);
  xor P3 (P3_out, a3, b3);
  and and_3 (and_3_out, P3_out, P2_out, P1_out, G0_out);
  and and_4 (P0_star, P3_out, P2_out, P1_out, P0_out);
  and G2 (G2_out, a2, b2);
  xor xor_1 (out3, P3_out, C3_out);
  or C3 (C3_out, G2_out, and_6_out, and_5_out, and_7_out);
  and and_5 (and_5_out, P2_out, P1_out, G0_out);
  and and_6 (and_6_out, P2_out, G1_out);
  xor P2 (P2_out, a2, b2);
  and and_7 (and_7_out, P2_out, P1_out, P0_out, C0);
  xor xor_2 (out2, P2_out, C2_out);
  or C2 (C2_out, G1_out, and_8_out, and_9_out);
  and and_8 (and_8_out, P1_out, G0_out);
  xor P1 (P1_out, a1, b1);
  and G1 (G1_out, a1, b1);
  and and_9 (and_9_out, P1_out, P0_out, C0);
  xor xor_3 (out1, P1_out, C1_out);
  or C1 (C1_out, G0_out, and_10_out);
  and and_10 (and_10_out, P0_out, C0);
  xor P0 (P0_out, a0, b0);
  and G0 (G0_out, a0, b0);
  xor xor_4 (out0, P0_out, C0);
endmodule
